// Logisim project project3.circ as structural Verilog: 1 circuit, main circuit main
module main (
  input  in_1
);

  wire and_1_out, and_2_out, and_3_out, and_4_out, and_5_out, and_6_out, and_7_out, and_8_out, and_9_out,
       and_10_out, Clock_out, d_ff_1_q, d_ff_2_q, d_ff_3_q, d_ff_4_q, not_1_out, not_2_out, or_1_out,
       or_2_out, or_3_out, or_4_out, or_5_out, or_6_out, or_7_out, or_8_out, or_9_out, or_10_out, or_11_out,
       or_12_out, or_13_out, S1_2_q, S1_q;

  or or_1 (or_1_out, and_10_out, and_6_out, and_7_out);
  and and_1 (and_1_out, in_1, ~S1_2_q, d_ff_4_q);  // AND_Gate
  and and_2 (and_2_out, in_1, S1_2_q, ~d_ff_4_q);  // AND_Gate
  and and_3 (and_3_out, in_1, S1_2_q, d_ff_4_q);
  and and_4 (and_4_out, in_1, ~S1_2_q, ~d_ff_4_q);  // AND_Gate
  or or_2 (or_2_out, and_10_out, and_6_out, and_8_out);
  or or_3 (or_3_out, and_9_out, and_6_out, and_7_out, and_8_out);
  or or_4 (or_4_out, or_2_out, and_2_out, and_1_out);
  or or_5 (or_5_out, or_1_out, and_2_out, and_4_out);
  Clock Clock (.out(Clock_out));
  D_Flip_Flop d_ff_1 (.D(or_3_out), .clk(Clock_out), .Q(d_ff_1_q));  // open: Qn, preset, reset
  D_Flip_Flop d_ff_2 (.D(or_4_out), .clk(Clock_out), .Q(d_ff_2_q));  // open: Qn, preset, reset
  D_Flip_Flop d_ff_3 (.D(or_5_out), .clk(Clock_out), .Q(d_ff_3_q));  // open: Qn, preset, reset
  not not_1 (not_1_out, Clock_out);
  D_Flip_Flop S1 (.D(d_ff_1_q), .clk(not_1_out), .Q(S1_q));  // open: Qn, preset, reset
  D_Flip_Flop S1_2 (.D(d_ff_2_q), .clk(not_1_out), .Q(S1_2_q));  // open: Qn, preset, reset
  D_Flip_Flop d_ff_4 (.D(d_ff_3_q), .clk(not_1_out), .Q(d_ff_4_q));  // open: Qn, preset, reset
  not not_2 (not_2_out, in_1);
  or or_6 (or_6_out, and_4_out, and_1_out);
  and and_5 (and_5_out, not_2_out, S1_2_q, d_ff_4_q, S1_q);
  and and_6 (and_6_out, not_2_out, ~S1_2_q, d_ff_4_q, S1_q);  // AND_Gate
  and and_7 (and_7_out, not_2_out, S1_2_q, ~d_ff_4_q, S1_q);  // AND_Gate
  and and_8 (and_8_out, not_2_out, ~S1_2_q, ~d_ff_4_q, S1_q);  // AND_Gate
  and and_9 (and_9_out, not_2_out, S1_2_q, d_ff_4_q, ~S1_q);  // AND_Gate
  and and_10 (and_10_out, not_2_out, ~S1_2_q, ~d_ff_4_q, ~S1_q);  // AND_Gate
  or or_7 (or_7_out, or_13_out, and_5_out, and_9_out, and_8_out, and_10_out);
  or or_8 (or_8_out, and_6_out, and_1_out);
  or or_9 (or_9_out, and_7_out, and_4_out);
  LED led_1 (.in(or_7_out));
  LED led_2 (.in(or_8_out));
  LED led_3 (.in(or_9_out));
  LED led_4 (.in(or_10_out));
  LED led_5 (.in(or_11_out));
  LED led_6 (.in(or_12_out));
  or or_10 (or_10_out, or_6_out, and_6_out, and_8_out, and_7_out, and_5_out);
  or or_11 (or_11_out, and_9_out, and_3_out);
  or or_12 (or_12_out, and_10_out, and_2_out);
  or or_13 (or_13_out, and_3_out, and_2_out);

  // Notes on the sheet:
  //   s01
  //   yellow red
  //   red green
  //   s10
  //   red yellow
  //   s11
  //   s00
  //   green red
  //   s111
  //   s101
  //   s011
  //   s001
  //   Red Yellow
  //   s110
  //   Red Green
  //   s000
  //   Red Red
  //   Yellow Red
  //   Green Red
  //   Red Red
endmodule
